# Fritzing sketch Potentiometer (saved by Fritzing 0.7.12b)
breadboards: 1

parts:
  Arduino1 = Arduino
  R1 = Rotary Potentiometer (Small) [maximum_resistance=100kΩ]
  S1 = Pushbutton [package="[THT]"]
  J1 = Piezo Speaker

nets:
  N1: Arduino1.GND, R1.leg2, S1.Pin_1, S1.Pin_2, J1.pin2
  N2: Arduino1.+5V, R1.leg1
  N3: Arduino1.A0, R1.wiper
  N4: S1.Pin_3, S1.Pin_4
