# Fritzing sketch Theremin (saved by Fritzing 0.7.12b)
breadboards: 1

parts:
  Arduino1 = Arduino
  R1 = Photocell (LDR) [package=THT]
  R2 = Resistor [tolerance=±5% resistance=220 package=THT]
  J1 = Piezo Speaker
  S1 = Pushbutton [package="[THT]"]

nets:
  N1: Arduino1.D9, J1.pin1
  N2: Arduino1.GND, R2.Pin_1, S1.Pin_3, S1.Pin_4
  N3: Arduino1.A0, R1.pin_1, R2.Pin_0
  N4: J1.pin2, S1.Pin_1, S1.Pin_2
